# Fritzing sketch GittCircuit (saved by Fritzing 0.8.7b)
breadboards: 1

parts:
  VCC1 = Battery
  M1 = DC Motor
  M2 = DC Motor
  Part1 = L298N
  Part2 = LPC4088
  Part3 = LM393
  M3 = DC Motor
  M4 = DC Motor
  Part4 = SRF05 Ultrasonic Rangefinder
  U1 = POT [package=pot_alpha_rv16af-20]
  Part5 = Bluetooth HM-10
  R1 = Photocell (LDR) [package=THT]
  R2 = Resistor [tolerance=±5% resistance=220 package=THT]
  R3 = Photocell (LDR) [package=THT]
  R4 = Resistor [tolerance=±5% resistance=220 package=THT]
  R5 = Resistor [tolerance=±5% resistance=220 package="0805 [SMD]"]
  LED1 = RGB LED - (4 legs) [package="5 mm [THT]"]
  LED2 = RGB LED - (4 legs) [package="5 mm [THT]"]
  LED4 = RGB LED - (4 legs) [package="5 mm [THT]"]
  R6 = Resistor [tolerance=±5% resistance=220 package="0805 [SMD]"]
  R7 = Resistor [tolerance=±5% resistance=220 package="0805 [SMD]"]
  R8 = Resistor [tolerance=±5% resistance=220 package="0805 [SMD]"]
  LED3 = RGB LED (com. cathode, rgb) [package="5 mm [THT]"]  # not connected

nets:
  N1: VCC1.-, Part1.GND, Part2.GND#0
  N2: VCC1.+, Part1.12V
  N3: M1.pin_1, M2.pin_1, Part1.MotorB2
  N4: M1.pin_2, M2.pin_2, Part1.MotorB1
  N5: Part1.MotorA1, M3.pin_1, M4.pin_1
  N6: Part1.MotorA2, M3.pin_2, M4.pin_2
  5V: Part1.5V, Part2.VIN
  N7: Part1.ENA, Part2.P28
  N8: Part1.IN1, Part2.P5
  N9: Part1.IN2, Part2.P6
  N10: Part1.IN3, Part2.P39
  N11: Part1.IN4, Part2.P38
  N12: Part1.ENB, Part2.P27
  N13: Part2.P8, Part3.OUT
  N14: Part2.P9, Part5.RXD
  N15: Part2.P10, Part5.TXD
  N16: Part2.P11, Part4.Trig
  N17: Part2.P15, R8.Pin_0
  N18: Part2.P16, Part4.Echo
  N19: Part2.P17, R1.pin_1, R2.Pin_0
  N20: Part2.P19, U1.S
  N21: Part2.P20, R3.pin_1, R4.Pin_0
  GND: Part2.GND#21, Part3.GND, Part4.GND, U1.E, Part5.GND, R1.pin_0, R3.pin_0, LED1.red_cathode, LED2.red_cathode, LED4.blue_cathode
  N22: Part2.VOUT, R2.Pin_1, R4.Pin_1
  VCC: Part2.VU, Part3.VCC, Part4.VCC, U1.A, Part5.VCC
  N23: Part2.P26, R6.Pin_1
  N24: Part2.P25, R5.Pin_1
  N25: Part2.P24, R7.Pin_0
  N26: R5.Pin_0, LED1.blue_cathode
  N27: LED2.blue_cathode, R6.Pin_0
  N28: LED4.red_cathode, R7.Pin_1

notes:
  Front Right
  Motor
  Front Left
  Back Right
  Back Left
  Left LDR
  Right LDR
  Front Right LED
  Front Left LED
  Back Left LED
  Back Right LED
